// Logisim project Project.circ as structural Verilog: 2 circuits, main circuit Chaser Gamer
module Chaser_Gamer (
  input  in_1,
  input  Reset,
  input  in_3,
  input  in_4,
  output out_5,
  output out_6,
  output out_7,
  output out_8,
  output out_9,
  output out_10
);

  wire and_5_out, and_8_out, and_9_out, and_10_out, and_11_out, and_12_out, and_13_out, and_14_out,
       and_15_out, button_1_out, button_2_out, button_3_out, clock_1_out, clock_2_out, j_k_ff_1_q,
       j_k_ff_1_qn, j_k_ff_2_q, j_k_ff_2_qn, j_k_ff_3_q, j_k_ff_3_qn, j_k_ff_4_q, j_k_ff_4_qn, j_k_ff_5_q,
       j_k_ff_5_qn, j_k_ff_6_q, j_k_ff_6_qn, j_k_ff_7_q, j_k_ff_7_qn, j_k_ff_8_q, j_k_ff_8_qn, j_k_ff_9_q,
       j_k_ff_9_qn, j_k_ff_10_q, j_k_ff_10_qn, j_k_ff_11_q, j_k_ff_11_qn, j_k_ff_12_q, j_k_ff_12_qn;
  wire [7:0] counter_1_q;

  Clock clock_1 (.out(clock_1_out));
  Counter counter_1 (.count(out_8), .Q(counter_1_q), .clk(clock_1_out), .clr(in_4));  // open: load, D, carry
  Clock clock_2 (.out(clock_2_out));
  Hex_Digit_Display hex_digit_display_1 (.value(counter_1_q[3:0]));  // open: dp
  Hex_Digit_Display hex_digit_display_2 (.value(counter_1_q[7:4]));  // open: dp
  J_K_Flip_Flop j_k_ff_1 (
    .J(Reset), .clk(clock_2_out), .K(Reset), .Q(j_k_ff_1_q), .Qn(j_k_ff_1_qn), .preset(and_5_out));  // open: en, reset
  J_K_Flip_Flop j_k_ff_2 (
    .J(Reset), .clk(j_k_ff_1_q), .K(Reset), .Q(j_k_ff_2_q), .Qn(j_k_ff_2_qn), .preset(and_5_out));  // open: en, reset
  J_K_Flip_Flop j_k_ff_3 (
    .J(Reset), .clk(j_k_ff_2_q), .K(Reset), .Q(j_k_ff_3_q), .Qn(j_k_ff_3_qn), .preset(and_5_out));  // open: en, reset
  and and_1 (out_8, out_5, button_1_out);
  and and_2 (out_8, and_9_out, button_2_out);
  and and_3 (out_8, and_12_out, button_3_out);
  J_K_Flip_Flop j_k_ff_4 (
    .J(Reset), .clk(j_k_ff_3_q), .K(Reset), .Q(j_k_ff_4_q), .Qn(j_k_ff_4_qn), .preset(and_5_out));  // open: en, reset
  and and_4 (out_5, j_k_ff_4_q, j_k_ff_3_q, j_k_ff_2_q, j_k_ff_1_q);
  and and_5 (and_5_out, j_k_ff_1_q, j_k_ff_2_q, j_k_ff_3_q, j_k_ff_4_qn);
  and and_6 (out_7, j_k_ff_4_q, j_k_ff_3_qn, j_k_ff_2_qn, j_k_ff_1_q);
  and and_7 (out_6, j_k_ff_4_q, j_k_ff_3_qn, j_k_ff_2_qn, j_k_ff_1_qn);
  LED led_1 (.in(and_11_out));
  LED led_2 (.in(out_7));
  LED led_3 (.in(out_6));
  LED led_4 (.in(and_8_out));
  LED led_5 (.in(out_5));
  LED led_6 (.in(and_9_out));
  Button button_1 (.out(button_1_out));
  Button button_2 (.out(button_2_out));
  LED led_7 (.in(and_15_out));
  LED led_8 (.in(and_14_out));
  LED led_9 (.in(and_12_out));
  Button button_3 (.out(button_3_out));
  J_K_Flip_Flop j_k_ff_5 (
    .J(in_3), .clk(clock_2_out), .K(in_3), .Q(j_k_ff_5_q), .Qn(j_k_ff_5_qn), .preset(and_10_out));  // open: en, reset
  J_K_Flip_Flop j_k_ff_6 (
    .J(in_3), .clk(j_k_ff_5_q), .K(in_3), .Q(j_k_ff_6_q), .Qn(j_k_ff_6_qn), .preset(and_10_out));  // open: en, reset
  J_K_Flip_Flop j_k_ff_7 (
    .J(in_3), .clk(j_k_ff_6_q), .K(in_3), .Q(j_k_ff_7_q), .Qn(j_k_ff_7_qn), .preset(and_10_out));  // open: en, reset
  J_K_Flip_Flop j_k_ff_8 (
    .J(in_3), .clk(j_k_ff_7_q), .K(in_3), .Q(j_k_ff_8_q), .Qn(j_k_ff_8_qn), .preset(and_10_out));  // open: en, reset
  and and_8 (and_8_out, j_k_ff_8_q, j_k_ff_7_qn, j_k_ff_6_qn, j_k_ff_5_qn);
  and and_9 (and_9_out, j_k_ff_8_q, j_k_ff_7_q, j_k_ff_6_q, j_k_ff_5_q);
  and and_10 (and_10_out, j_k_ff_5_q, j_k_ff_6_q, j_k_ff_7_q, j_k_ff_8_qn);
  and and_11 (and_11_out, j_k_ff_8_q, j_k_ff_7_qn, j_k_ff_6_qn, j_k_ff_5_q);
  J_K_Flip_Flop j_k_ff_9 (
    .J(in_1), .clk(clock_2_out), .K(in_1), .Q(j_k_ff_9_q), .Qn(j_k_ff_9_qn), .preset(and_13_out));  // open: en, reset
  J_K_Flip_Flop j_k_ff_10 (
    .J(in_1), .clk(j_k_ff_9_q), .K(in_1), .Q(j_k_ff_10_q), .Qn(j_k_ff_10_qn), .preset(and_13_out));  // open: en, reset
  J_K_Flip_Flop j_k_ff_11 (
    .J(in_1), .clk(j_k_ff_10_q), .K(in_1), .Q(j_k_ff_11_q), .Qn(j_k_ff_11_qn), .preset(and_13_out));  // open: en, reset
  J_K_Flip_Flop j_k_ff_12 (
    .J(in_1), .clk(j_k_ff_11_q), .K(in_1), .Q(j_k_ff_12_q), .Qn(j_k_ff_12_qn), .preset(and_13_out));  // open: en, reset
  and and_12 (and_12_out, j_k_ff_12_q, j_k_ff_11_q, j_k_ff_10_q, j_k_ff_9_q);
  and and_13 (and_13_out, j_k_ff_9_q, j_k_ff_10_q, j_k_ff_11_q, j_k_ff_12_qn);
  and and_14 (and_14_out, j_k_ff_12_q, j_k_ff_11_qn, j_k_ff_10_qn, j_k_ff_9_qn);
  and and_15 (and_15_out, j_k_ff_12_q, j_k_ff_11_qn, j_k_ff_10_qn, j_k_ff_9_q);

  assign out_9 = out_8;
  assign out_10 = out_8;

  // Notes on the sheet:
  //   Counter
  //   Clock
  //   Displa
  //   JK FLIP FLOP
  //   LEDs
  //   PUsh Button
endmodule

module counter (
  input  in_1,
  input  in_2
);

  wire clock_1_out;
  wire [7:0] counter_1_q;

  Clock clock_1 (.out(clock_1_out));
  Counter counter_1 (.count(in_1), .Q(counter_1_q), .clk(clock_1_out), .clr(in_2));  // open: load, D, carry
  Hex_Digit_Display hex_digit_display_1 (.value(counter_1_q[7:4]));  // open: dp
  Hex_Digit_Display hex_digit_display_2 (.value(counter_1_q[3:0]));  // open: dp
endmodule
